# Fritzing sketch autoToll (saved by Fritzing 0.9.2b)
breadboards: 1

parts:
  R1 = Resistor [tolerance=±5% resistance=220 package=THT]
  U1 = ESP8266 WiFi Module [part_number=ESP8266]
  U2 = V_REG_LD1117VXX [package=78xxl]
  Part1 = RFID USB Reader
  R2 = Resistor [tolerance=±5% resistance=220 package=THT]
  C2 = Ceramic Capacitor [capacitance=0.1µF package="100 mil [THT, multilayer]"]
  C3 = Electrolytic Capacitor [capacitance=100µF package="200 mil [THT, electrolytic]"]

nets:
  N1: R1.Pin_0, Part1.TX-O
  N2: R1.Pin_1, U1.RXD, R2.Pin_0
  N3: U1.VCC, U1.CH_PD, U2.OUT
  GND: U1.GND, Part1.GND, C2.0, C3.-
  GND_2: U2.GND, R2.Pin_1
  5V: U2.IN, Part1.VCC, C2.1, C3.+

notes:
  WIRELESS MODULE
  3.3V REGULATOR
  LM1117
  VCC
  GND
  RFID READER MODULE
  VOLTAGE DIVIDER
  5V
  3.3V
  AUTOMATED TOLL BOOTH SYSTEM

custom parts:
  ESP8266 WiFi Module: Generic WiFi Module based on the ESP8266 with onboard PCB antenna and UART communications
